# Fritzing sketch MobileInc (saved by Fritzing 0.9.3b)
breadboards: 1

parts:
  DHT1 = DHT11 Humitidy and Temperature Sensor
  R1 = Resistor [tolerance=±5% resistance=330 package="2512 [SMD]"]
  R3 = Resistor [tolerance=±5% resistance=330 package="2512 [SMD]"]
  R4 = Resistor [tolerance=±5% resistance=330 package="2512 [SMD]"]
  R5 = Resistor [tolerance=±5% resistance=330 package="2512 [SMD]"]
  R6 = Resistor [tolerance=±5% resistance=330 package="2512 [SMD]"]
  R7 = Resistor [tolerance=±5% resistance=330 package="2512 [SMD]"]
  R8 = Resistor [tolerance=±5% resistance=330 package="2512 [SMD]"]
  R9 = Resistor [tolerance=±5% resistance=330 package="2512 [SMD]"]
  Part1 = Arduino Uno (Rev3) - ICSP
  LED2 = LED - 5mm [color="Green (570nm)" package="5 mm [THT]"]
  U1 = 74HC595 [package="DIP16 [THT]"]
  U2 = LCD-16X2 [package=lcd-16x2_noholes]
  LCM1602_IIC1 = LCM1602 IIC [part_number="LCM1602 IIC" chip_label="LCM1602 IIC" package="DIP (Dual Inline) [THT]"]
  S2 = Pushbutton [package="[SMD]"]
  LED1 = LED - 5mm [color="Red (633nm)" package="5 mm [THT]"]
  DI1 = 7-Segment LED Display [package=THT]
  R2 = Resistor [tolerance=±5% resistance=330 package="2512 [SMD]"]

nets:
  VCC: DHT1.VDD, R9.Pin_1, Part1.5V, U1.MR, U1.VCC, LCM1602_IIC1.VCC, DI1.commAnode#2
  N1: DHT1.DATA, R9.Pin_0, Part1.D8
  GND: DHT1.GND, Part1.GND, LED2.cathode, U1.GND, U1.OE, LCM1602_IIC1.GND, S2.Pin_3, S2.Pin_4, LED1.cathode
  N2: R1.Pin_0, R1.Pin_1, U1.Q2, DI1.cathodeC
  N3: R3.Pin_0, R3.Pin_1, U1.Q7, DI1.cathodeDP
  N4: R4.Pin_0, R4.Pin_1, U1.Q0, DI1.cathodeB
  N5: R5.Pin_0, R5.Pin_1, U1.Q5, DI1.cathodeF
  N6: R6.Pin_0, R6.Pin_1, U1.Q3, DI1.cathodeD
  N7: R7.Pin_0, R7.Pin_1, U1.Q4, DI1.cathodeE
  N8: R8.Pin_0, R8.Pin_1, U1.Q6, DI1.cathodeG
  N9: Part1.A4/SDA, LCM1602_IIC1.SDA
  N10: Part1.A5/SCL, LCM1602_IIC1.SCL
  N11: Part1.D10_PWM/SS, LED1.anode
  N12: Part1.D12/MISO, S2.Pin_1, S2.Pin_2
  N13: Part1.D13/SCK, LED2.anode
  N14: Part1.D5_PWM, U1.DS
  N15: Part1.D6_PWM, U1.ST_CP
  N16: Part1.D7, U1.SH_CP
  N17: U1.Q1, DI1.cathodeA, R2.Pin_0, R2.Pin_1
  VSS: U2.VSS, LCM1602_IIC1.VSS
  VDD: U2.VDD, LCM1602_IIC1.VDD
  N18: U2.VO, LCM1602_IIC1.V0
  N19: U2.RS, LCM1602_IIC1.RS
  N20: U2.R_W, LCM1602_IIC1.RW
  N21: U2.E, LCM1602_IIC1.E
  N22: U2.DB0, LCM1602_IIC1.D0
  N23: U2.DB1, LCM1602_IIC1.D1
  N24: U2.DB2, LCM1602_IIC1.D2
  N25: U2.DB3, LCM1602_IIC1.D3
  N26: U2.DB4, LCM1602_IIC1.D4
  N27: U2.DB5, LCM1602_IIC1.D5
  N28: U2.DB6, LCM1602_IIC1.D6
  N29: U2.DB7, LCM1602_IIC1.D7
  N30: U2.A, LCM1602_IIC1.A
  N31: U2.K, LCM1602_IIC1.K

custom parts:
  DHT11 Humitidy and Temperature Sensor: DHT11 Humidity and Temperature Sensor
  LCM1602 IIC: I2C-Module to use a 1602 or 2004 LCD on with the wire.h libory Serial LCD Modul
